# Fritzing sketch wired (saved by Fritzing 0.9.3b)

parts:
  obniz1 = obniz
  8x8_LED_Modul_mit_MAX1 = 8x8 LED Modul mit MAX7219 [package=THT]
  8x8_LED_Modul_mit_MAX2 = 8x8 LED Modul mit MAX7219 [package=THT]

nets:
  N1: obniz1.io0, 8x8_LED_Modul_mit_MAX1.CLK_Eingang
  N2: obniz1.io1, 8x8_LED_Modul_mit_MAX1.CS_Eingang
  N3: obniz1.io2, 8x8_LED_Modul_mit_MAX1.DIN_Eingang
  N4: obniz1.io3, 8x8_LED_Modul_mit_MAX1.GND_Eingang
  N5: obniz1.io4, 8x8_LED_Modul_mit_MAX1.VCC_Eingang
  N6: 8x8_LED_Modul_mit_MAX1.VCC_Ausgang, 8x8_LED_Modul_mit_MAX2.VCC_Eingang
  N7: 8x8_LED_Modul_mit_MAX1.GND_Ausgang, 8x8_LED_Modul_mit_MAX2.GND_Eingang
  N8: 8x8_LED_Modul_mit_MAX1.DOUT_Ausgang, 8x8_LED_Modul_mit_MAX2.DIN_Eingang
  N9: 8x8_LED_Modul_mit_MAX1.CS_Ausgang, 8x8_LED_Modul_mit_MAX2.CS_Eingang
  N10: 8x8_LED_Modul_mit_MAX1.CLK_Ausgang, 8x8_LED_Modul_mit_MAX2.CLK_Eingang

custom parts:
  obniz: obniz is a microcontroller board based
