# Fritzing sketch potentiometer (saved by Fritzing 0.9.3b)

parts:
  obniz1 = obniz
  U1 = POT [package=pot_mammoth]

nets:
  N1: obniz1.io0, U1.E
  N2: obniz1.io1, U1.A
  N3: obniz1.io2, U1.S

custom parts:
  obniz: obniz is a microcontroller board based
