# Fritzing sketch AE_MICAMP (saved by Fritzing 0.9.3b)

parts:
  obniz1 = obniz
  パーツ2 = Adafruit MAX4466 Electret Microphone Amplifier [part_number="Adafruit #1063"]

nets:
  N1: obniz1.io0, パーツ2.VCC
  N2: obniz1.io1, パーツ2.GND
  N3: obniz1.io2, パーツ2.OUT

custom parts:
  obniz: obniz is a microcontroller board based
  Adafruit MAX4466 Electret Microphone Amplifier: Add an ear to your project with this well-designed electret microphone amplifier. This fully assembled and tested board comes with a 20-20KHz electret microphone soldered on. For the amplification, we use the Maxim MAX4466, an op-amp specifically designed for this delicate task! The amplifier has excellent power supply noise rejection, so this amplifier sounds really good and isn't nearly as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
