# Fritzing sketch wired (saved by Fritzing 0.9.3b)
breadboards: 1

parts:
  obniz1 = obniz
  U1 = XBEE-1 [package=xbee-1_lock]
  U2 = Voltage Regulator [package=to-92]

nets (from the breadboard view):
  N1: obniz1.io8, U1.GND, U2.IN
  N2: obniz1.io9, U1.DIN
  N3: obniz1.io10, U1.DOUT
  N4: obniz1.io11, U2.GND
  N5: U1.VDD, U2.OUT

custom parts:
  obniz: obniz is a microcontroller board based
