# Fritzing sketch wired (saved by Fritzing 0.9.3b)
breadboards: 1

parts:
  7_Segment1 = 7 Segment Display
  obniz1 = obniz

nets:
  N1: 7_Segment1.Segment_E, obniz1.io3
  N2: 7_Segment1.Segment_D, obniz1.io2
  N3: 7_Segment1.common_cathode, obniz1.io6
  N4: 7_Segment1.Segment_C, obniz1.io1
  N5: 7_Segment1.Segment_DP, obniz1.io0
  N6: 7_Segment1.Segment_B, obniz1.io8
  N7: 7_Segment1.Segment_A, obniz1.io7
  N8: 7_Segment1.Segment_F, obniz1.io5
  N9: 7_Segment1.Segment_G, obniz1.io4

notes:
  g  f      a  b
  e  d      c  dp
  com

custom parts:
  obniz: obniz is a microcontroller board based
