# Fritzing sketch wired (saved by Fritzing 0.9.3b)
breadboards: 1

parts:
  obniz1 = obniz
  7_Segment1 = 7 Segment Display
  7_Segment2 = 7 Segment Display
  7_Segment3 = 7 Segment Display
  7_Segment4 = 7 Segment Display

nets:
  N1: obniz1.io0, 7_Segment1.Segment_E, 7_Segment2.Segment_E, 7_Segment3.Segment_E, 7_Segment4.Segment_E
  N2: obniz1.io1, 7_Segment1.Segment_D, 7_Segment2.Segment_D, 7_Segment3.Segment_D, 7_Segment4.Segment_D
  N3: obniz1.io2, 7_Segment1.Segment_C, 7_Segment2.Segment_C, 7_Segment3.Segment_C, 7_Segment4.Segment_C
  N4: obniz1.io3, 7_Segment1.Segment_DP, 7_Segment2.Segment_DP, 7_Segment3.Segment_DP, 7_Segment4.Segment_DP
  N5: obniz1.io4, 7_Segment1.Segment_G, 7_Segment2.Segment_G, 7_Segment3.Segment_G, 7_Segment4.Segment_G
  N6: obniz1.io5, 7_Segment1.Segment_F, 7_Segment2.Segment_F, 7_Segment3.Segment_F, 7_Segment4.Segment_F
  N7: obniz1.io6, 7_Segment1.Segment_A, 7_Segment2.Segment_A, 7_Segment3.Segment_A, 7_Segment4.Segment_A
  N8: obniz1.io7, 7_Segment1.Segment_B, 7_Segment2.Segment_B, 7_Segment3.Segment_B, 7_Segment4.Segment_B
  N9: obniz1.io8, 7_Segment1.common_cathode
  N10: obniz1.io9, 7_Segment2.common_cathode
  N11: obniz1.io10, 7_Segment3.common_cathode
  N12: obniz1.io11, 7_Segment4.common_cathode

custom parts:
  obniz: obniz is a microcontroller board based
