# Fritzing sketch gp2y0a21yk0f (saved by Fritzing 0.9.3b)

parts:
  obniz1 = obniz
  J1 = Infrared Proximity Sensor

nets:
  N1: obniz1.io0, J1.Vcc
  N2: obniz1.io1, J1.GND
  N3: obniz1.io2, J1.Vout

custom parts:
  obniz: obniz is a microcontroller board based
