# Fritzing sketch wired (saved by Fritzing 0.9.3b)

parts:
  obniz1 = obniz
  hc-sr1 = hc-sr04

nets:
  N1: obniz1.io0, hc-sr1.GND
  N2: obniz1.io1, hc-sr1.Echo
  N3: obniz1.io2, hc-sr1.Trig
  N4: obniz1.io3, hc-sr1.VCC

custom parts:
  obniz: obniz is a microcontroller board based
