# Fritzing sketch infraredled (saved by Fritzing 0.9.3b)
breadboards: 1

parts:
  obniz1 = obniz
  LED1 = smd LED [color="Infrared (880nm)" package="0805 [SMD]"]
  R1 = Resistor [tolerance=±5% resistance=220 package=THT]

nets:
  N1: obniz1.io0, R1.Pin_0
  N2: obniz1.io1, LED1.cathode
  N3: LED1.anode, R1.Pin_1

custom parts:
  obniz: obniz is a microcontroller board based
