# Fritzing sketch wired (saved by Fritzing 0.9.3b)

parts:
  obniz1 = obniz
  LED1 = LED - 5mm [color="Red (635nm)" package="5 mm [THT]"]

nets:
  N1: obniz1.io0, LED1.anode
  N2: obniz1.io1, LED1.cathode

custom parts:
  obniz: obniz is a microcontroller board based
