# Fritzing sketch wired (saved by Fritzing 0.9.3b)

parts:
  obniz1 = obniz
  S2 = Round Pushbutton

nets:
  N1: obniz1.io0, S2.leg1
  N2: obniz1.io1, S2.leg0

custom parts:
  obniz: obniz is a microcontroller board based
