# Fritzing sketch wired (saved by Fritzing 0.9.3b)

parts:
  obniz1 = obniz
  パーツ1 = Thumb Joystick

nets:
  N1: obniz1.io0, パーツ1.GND
  N2: obniz1.io1, パーツ1.SEL
  N3: obniz1.io2, パーツ1.HORZ
  N4: obniz1.io3, パーツ1.VERT
  N5: obniz1.io4, パーツ1.VCC

custom parts:
  obniz: obniz is a microcontroller board based
