# Fritzing sketch wired (saved by Fritzing 0.9.3b)

parts:
  obniz1 = obniz
  J1 = Basic Servo

nets:
  N1: obniz1.io0, J1.pulse
  N2: obniz1.io1, J1.vcc
  N3: obniz1.io2, J1.gnd

custom parts:
  obniz: obniz is a microcontroller board based
