# Fritzing sketch solenoid (saved by Fritzing 0.9.3b)

parts:
  obniz1 = obniz
  L1 = Solenoid

nets:
  N1: obniz1.io0, L1.pin1
  N2: obniz1.io1, L1.pin2

custom parts:
  obniz: obniz is a microcontroller board based
