# Fritzing sketch wired (saved by Fritzing 0.9.3b)

parts:
  obniz1 = obniz
  J1 = Piezo Speaker

nets:
  N1: obniz1.io0, J1.pin2
  N2: obniz1.io1, J1.pin1

custom parts:
  obniz: obniz is a microcontroller board based
