# Fritzing sketch wired (saved by Fritzing 0.9.3b)
breadboards: 1

parts:
  obniz1 = obniz
  IC1 = IC, DIP package, 4 pins

nets:
  N1: obniz1.io0, IC1.pin1
  N2: obniz1.io1, IC1.pin4
  N3: obniz1.io2, IC1.pin2

custom parts:
  obniz: obniz is a microcontroller board based
