# Fritzing sketch wired (saved by Fritzing 0.9.3b)
breadboards: 1

parts:
  obniz1 = obniz
  IC1 = IC, DIP package, 8 pins [chip_label=ADT7310]

nets:
  N1: obniz1.io0, IC1.pin8
  N2: obniz1.io1, IC1.pin7
  N3: obniz1.io2, IC1.pin6
  N4: obniz1.io3, IC1.pin5
  N5: obniz1.io5, IC1.pin4
  N6: obniz1.io6, IC1.pin3
  N7: obniz1.io7, IC1.pin2
  N8: obniz1.io8, IC1.pin1

notes:
  1pinから
  1 SCLK
  2 DOUT
  3 DIN
  4 CS
  5 INT
  6 CT
  7 GND
  8 VDD

custom parts:
  obniz: obniz is a microcontroller board based
