# Fritzing sketch JpegSerialCam (saved by Fritzing 0.9.3b)

parts:
  obniz1 = obniz
  CAMERA1 = TTL Serial JPEG Camera

nets:
  N1: obniz1.io0, CAMERA1.5V
  N2: obniz1.io1, CAMERA1.RX
  N3: obniz1.io2, CAMERA1.TX
  N4: obniz1.io3, CAMERA1.GND

custom parts:
  obniz: obniz is a microcontroller board based
  TTL Serial JPEG Camera: TTL Serial JPEG Camera with NTSC Out
