# Fritzing sketch wired (saved by Fritzing 0.9.3b)
breadboards: 1

parts:
  7_Segment1 = 7 Segment Display
  obniz1 = obniz
  R1 = Resistor [tolerance=±5% resistance=220 package=THT]
  R2 = Resistor [tolerance=±5% resistance=220 package=THT]
  R3 = Resistor [tolerance=±5% resistance=220 package=THT]
  R4 = Resistor [tolerance=±5% resistance=220 package=THT]
  R5 = Resistor [tolerance=±5% resistance=220 package=THT]
  R6 = Resistor [tolerance=±5% resistance=220 package=THT]
  R7 = Resistor [tolerance=±5% resistance=220 package=THT]
  R8 = Resistor [tolerance=±5% resistance=220 package=THT]

nets (from the breadboard view):
  N1: 7_Segment1.Segment_E, R3.Pin_1
  N2: 7_Segment1.Segment_D, R4.Pin_1
  N3: 7_Segment1.common_cathode, obniz1.io4
  N4: 7_Segment1.Segment_C, R8.Pin_0
  N5: 7_Segment1.Segment_DP, R5.Pin_0
  N6: 7_Segment1.Segment_B, R2.Pin_0
  N7: 7_Segment1.Segment_A, R1.Pin_0
  N8: 7_Segment1.Segment_F, R7.Pin_1
  N9: 7_Segment1.Segment_G, R6.Pin_1
  N10: obniz1.io0, R3.Pin_0
  N11: obniz1.io1, R4.Pin_0
  N12: obniz1.io2, R6.Pin_0
  N13: obniz1.io3, R7.Pin_0
  N14: obniz1.io5, R1.Pin_1
  N15: obniz1.io6, R2.Pin_1
  N16: obniz1.io7, R8.Pin_1
  N17: obniz1.io8, R5.Pin_1

notes:
  g  f      a  b
  e  d      c  dp
  com

custom parts:
  obniz: obniz is a microcontroller board based
