# Fritzing sketch obniz-max7219 (saved by Fritzing 0.9.3b)
breadboards: 1

parts:
  IC1 = IC, DIP package, 24 pins [chip_label=MAX7219]
  obniz1 = obniz
  R1 = Resistor [tolerance=±5% resistance=33k package=THT]
  IC2 = IC, DIP package, 24 pins [chip_label=MAX7219]
  R2 = Resistor [tolerance=±5% resistance=33k package=THT]
  C1 = Ceramic Capacitor [capacitance=100nF package="100 mil [THT, multilayer]"]
  C2 = Ceramic Capacitor [capacitance=100nF package="100 mil [THT, multilayer]"]

nets:
  N1: IC1.pin1, obniz1.io2
  N2: IC1.pin4, IC1.pin9, obniz1.io3, IC2.pin4, IC2.pin9, C1.0, C2.0
  N3: IC1.pin12, obniz1.io1, IC2.pin12
  N4: IC1.pin13, obniz1.io0, IC2.pin13
  N5: IC1.pin18, R1.Pin_1
  N6: IC1.pin19, obniz1.io4, R1.Pin_0, IC2.pin19, R2.Pin_0, C1.1, C2.1
  N7: IC1.pin24, IC2.pin1
  N8: IC2.pin18, R2.Pin_1

custom parts:
  obniz: obniz is a microcontroller board based
