# Fritzing sketch wired (saved by Fritzing 0.9.3b)
breadboards: 1

parts:
  obniz1 = obniz
  LED2 = RGB LED (com. cathode, rbg) [color="Red (633nm)" package="5 mm [THT]"]
  R1 = Resistor [tolerance=±5% resistance=220 package=THT]
  R2 = Resistor [tolerance=±5% resistance=220 package=THT]
  R3 = Resistor [tolerance=±5% resistance=220 package=THT]

nets:
  N1: obniz1.io0, R1.Pin_1
  N2: obniz1.io1, R2.Pin_1
  N3: obniz1.io2, LED2.common_cathode
  N4: obniz1.io3, R3.Pin_1
  N5: LED2.red_anode, R3.Pin_0
  N6: LED2.blue_anode, R2.Pin_0
  N7: LED2.green_anode, R1.Pin_0

custom parts:
  obniz: obniz is a microcontroller board based
