# Fritzing sketch WS2811 (saved by Fritzing 0.9.3b)
breadboards: 1

parts:
  obniz1 = obniz
  LED3 = RGB LED (com. anode, rbg) [package="5 mm [THT]"]
  LED4 = RGB LED (com. anode, rbg) [package="5 mm [THT]"]

nets:
  N1: obniz1.io0, LED3.blue_cathode, LED4.blue_cathode
  N2: obniz1.io1, LED3.common_anode, LED4.common_anode
  N3: obniz1.io2, LED3.red_cathode
  N4: LED3.green_cathode, LED4.red_cathode

custom parts:
  obniz: obniz is a microcontroller board based
