# Fritzing sketch SNx4HC595 (saved by Fritzing 0.9.3b)
breadboards: 1

parts:
  obniz1 = obniz
  IC1 = IC, DIP package, 16 pins [chip_label=IC]
  IC2 = IC, DIP package, 16 pins [chip_label=IC]

nets:
  N1: obniz1.io0, IC1.pin8, IC1.pin13, IC2.pin8, IC2.pin13
  N2: obniz1.io1, IC1.pin10, IC1.pin16, IC2.pin10, IC2.pin16
  N3: obniz1.io2, IC1.pin14
  N4: obniz1.io3, IC1.pin12, IC2.pin12
  N5: obniz1.io4, IC1.pin11, IC2.pin11
  N6: IC1.pin9, IC2.pin14

notes:
  Qb  Qc  Qd  Qe  Qf  Qg  Qh
  GND
  Vcc
  Qa
  SER
  OE
  RCLK
  SRCLK
  SRCLR
  Qh'

custom parts:
  obniz: obniz is a microcontroller board based
