# Fritzing sketch wired (saved by Fritzing 0.9.3b)

parts:
  obniz1 = obniz
  M1 = DC Motor

nets:
  N1: obniz1.io0, M1.pin_2
  N2: obniz1.io1, M1.pin_1

custom parts:
  obniz: obniz is a microcontroller board based
