# Fritzing sketch wired (saved by Fritzing 0.9.3b)

parts:
  obniz1 = obniz
  J1 = Basic Force Sensing Resistor (FSR) [package=THT]

nets:
  N1: obniz1.io0, J1.pin_1
  N2: obniz1.io1, J1.pin_0

custom parts:
  obniz: obniz is a microcontroller board based
