# Fritzing sketch SEN0114 (saved by Fritzing 0.9.3b)

parts:
  obniz1 = obniz
  パーツ1 = Soil Moisture Sensor

nets:
  N1: obniz1.io0, パーツ1.VCC
  N2: obniz1.io1, パーツ1.GND
  N3: obniz1.io2, パーツ1.SIG

custom parts:
  obniz: obniz is a microcontroller board based
