# Fritzing sketch wired (saved by Fritzing 0.9.3b)

parts:
  obniz1 = obniz
  T1 = LM35 Temperature Sensor [package="TO92 [THT]"]

nets:
  N1: obniz1.io0, T1.GND
  N2: obniz1.io1, T1.Vout
  N3: obniz1.io2, T1.+Vs

custom parts:
  obniz: obniz is a microcontroller board based
